# Fritzing sketch AM_Radio_Morse_Gemma (saved by Fritzing 0.9.3b)

parts:
  Part1 = Adafruit Gemma M0 [part_number="Adafruit #3501"]
  S1 = Pushbutton [package=THT]
  S2 = Pushbutton [package=THT]

nets:
  N1: Part1.D0_SDA_TX, S2.leg1
  N2: Part1.D2_SCL_RX, S1.leg0
  N3: Part1.GND, S1.leg1, S2.leg0

notes:
  'Dash'
  'Dot'
  antenna

custom parts:
  Adafruit Gemma M0: The Adafruit Gemma M0 is a super small microcontroller board, with just enough built-in to create many simple projects. It may look small and cute: round, about the size of a quarter, with friendly alligator-clip sew pads. But do not be fooled! The Gemma M0 is incredibly powerful! We've taken the same form factor we used for the original ATtiny85-based Gemma and gave it an upgrade. The Gemma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
