# Fritzing sketch m0_bme680_i2c (saved by Fritzing 0.9.3b)
breadboards: 1

parts:
  Part1 = Adafruit Feather M0 Basic Proto [part_number="Adafruit #2772"]
  Part4 = Adafruit BME680

nets:
  GND: Part1.GND, Part4.GND
  +3V3: Part1.+3V3, Part4.VIN
  N1: Part1.SCL, Part4.SCK/SCL
  N2: Part1.SDA, Part4.SDI/SDA

custom parts:
  Adafruit Feather M0 Basic Proto: At the Feather M0's heart is an ATSAMD21G18 ARM Cortex M0 processor, clocked at 48 MHz and at 3.3V logic, the same one used in the new Arduino Zero. This chip has a whopping 256K of FLASH (8x more than the Atmega328 or 32u4) and 32K of RAM (16x as much)! This chip comes with built in USB so it has USB-to-Serial program & debug capability built in with no need for an FTDI-like chip. To make it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
