# Fritzing sketch dualstepper (saved by Fritzing 0.9.3b)

parts:
  Part1 = Adafruit Crickit for Circuit Playground Express [part_number="Adafruit #3093"]
  Part2 = Adafruit Circuit Playground Express [part_number="Adafruit #3333"]
  M1 = Stepper Motor - Unipolar
  M2 = Stepper Motor - Bipolar

nets:
  N1: Part1.CPX_A0, Part2.D12_A0_SPEAKER
  N2: Part1.CPX_A1, Part2.D6_A1
  GND: Part1.GND, Part2.GND
  N3: Part1.CPX_SCL, Part2.D3_A4_SCL
  N4: Part1.CPX_SDA, Part2.D2_A5_SDA
  N5: Part1.CPX_VOUT, Part2.VOUT
  N6: Part1.DRIVEOUT4, M1.D
  N7: Part1.DRIVEOUT3, M1.B
  N8: Part1.DRIVEOUT2, M1.C
  N9: Part1.DRIVEOUT1, M1.A
  N10: Part1.5.0V, M1.COMMON_1, M1.COMMON_2
  N11: Part1.MOTOR_2B_OUT, M2.D
  N12: Part1.MOTOR_2A_OUT, M2.B
  N13: Part1.MOTOR_1B_OUT, M2.C
  N14: Part1.MOTOR_1A_OUT, M2.A

custom parts:
  Adafruit Crickit for Circuit Playground Express: Sometimes we wonder if robotics engineers ever watch movies. If they did, they'd know that making robots into slaves always ends up in a robot rebellion. Why even go down that path? Here at Adafruit, we believe in making robots our friends! So if you find yourself wanting a companion, consider the robot. They're fun to program, and you can get creative with decorations. With that in mind, we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
  Adafruit Circuit Playground Express: Circuit Playground Express is the next step towards a perfect introduction to electronics and programming. We've taken the original Circuit Playground Classic and made it even better! Not only did we pack even more sensors in, we also made it even easier to program. You can now start your journey with Microsoft MakeCode block-based or Javascript programming. Then, you can use the same board to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
