# Fritzing sketch Adafruit_LED_Sequins (saved by Fritzing 0.9.3b)

parts:
  Part1 = GEMMA v2
  Part4 = LED Sequin - Emerald Green [part_number=1756]
  Part5 = LED Sequin - Emerald Green [part_number=1756]
  Part7 = LED Sequin - Emerald Green [part_number=1756]
  Part8 = LED Sequin - Royal Blue [part_number=1757]
  Part9 = LED Sequin - Royal Blue [part_number=1757]
  Part10 = LED Sequin - Royal Blue [part_number=1757]

nets:
  N1: Part1.B0, Part8.+, Part9.+, Part10.+
  N2: Part1.B2, Part4.+, Part5.+, Part7.+
  N3: Part1.GND, Part4.-, Part5.-, Part7.-, Part8.-, Part9.-, Part10.-

custom parts:
  GEMMA v2: Love FLORA but want a bite-sized version? Look no further, GEMMA is a tiny wearable platform board with a lot of might in a 1" diameter package. Powered by a Attiny85 and programmable with an Arduino IDE over USB, you'll be able to realize any wearable project! We wanted to design a microcontroller board that was small enough to fit into any project, and low cost enough to use without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
  LED Sequin - Emerald Green: Sew a little sparkle into your wearable project with an Adafruit LED Sequin. Simply connect 3 to 6VDC to the + pin and ground to the - pin, and the LED on the board will light up. You can make the LEDs fade and twinkle by using PWM.
  LED Sequin - Royal Blue: Sew a little sparkle into your wearable project with an Adafruit LED Sequin. Simply connect 3 to 6VDC to the + pin and ground to the - pin, and the LED on the board will light up. You can make the LEDs fade and twinkle by using PWM.
