# Fritzing sketch FeatherM0MAX98357 (saved by Fritzing 0.9.3b)
breadboards: 1

parts:
  Part1 = Adafruit Feather M0 Express [part_number="Adafruit #3403"]
  Part2 = Adafruit MAX98357A I2S 3W Class D Amplifier [part_number="Adafruit #3006"]

nets:
  GND: Part1.GND, Part2.GND
  N1: Part1.TX, Part2.BCLK
  N2: Part1.RX, Part2.LRCLK
  +3V3: Part1.+3V3, Part2.VIN
  N3: Part1.D9, Part2.DIN

custom parts:
  Adafruit Feather M0 Express: We love all our Feathers equally, but this Feather is very special. It's our first Feather that is specifically designed for use with CircuitPython! CircuitPython is our beginner-oriented flavor of MicroPython - and as the name hints at, its a small but full-featured version of the popular Python programming language specifically for use with circuitry and electronics. That doesn't mean you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
  Adafruit MAX98357A I2S 3W Class D Amplifier: Listen to this good news - we now have an all in one digital audio amp breakout board that works incredibly well with the Raspberry Pi! If you're looking for an easy and low cost way to get you digital sound files bumpin' then the MAX08357 I2S Amp Breakout is for you. It takes standard I2S digital audio input and, not only decodes it into analog, but also amplifies it directly into a speaker.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
