# Fritzing sketch FeatherM4MAX98357 (saved by Fritzing 0.9.3b)
breadboards: 1

parts:
  Part1 = Adafruit Feather M4 Express [part_number="Adafruit #3857"]
  Part2 = Adafruit MAX98357A I2S 3W Class D Amplifier [part_number="Adafruit #3006"]

nets:
  N1: Part1.TX_D1, Part1.D11, Part2.DIN
  N2: Part1.A0, Part2.GND
  +3V3: Part1.+3V3, Part2.VIN
  N3: Part1.D10, Part2.LRCLK

custom parts:
  Adafruit Feather M4 Express: It's what you've been waiting for, the Feather M4 Express featuring ATSAMD51. This Feather is fast like a swift, smart like an owl, strong like a ox-bird (it's half ox, half bird, OK?) This feather is powered by our new favorite chip, the ATSAMD51J19 - with its 120MHz Cortex M4 with floating point support and 512KB Flash and 192KB RAM. Your code will zig and zag and zoom, and with a bunch of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
  Adafruit MAX98357A I2S 3W Class D Amplifier: Listen to this good news - we now have an all in one digital audio amp breakout board that works incredibly well with the Raspberry Pi! If you're looking for an easy and low cost way to get you digital sound files bumpin' then the MAX08357 I2S Amp Breakout is for you. It takes standard I2S digital audio input and, not only decodes it into analog, but also amplifies it directly into a speaker.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
