# Fritzing sketch MetroM0MAX98357 (saved by Fritzing 0.9.3b)
breadboards: 1

parts:
  Part5 = Adafruit Metro M0 Express
  Part6 = Adafruit MAX98357A I2S 3W Class D Amplifier [part_number="Adafruit #3006"]

nets:
  GND: Part5.GND, Part6.GND
  N1: Part5.D9, Part6.DIN
  N2: Part5.D1, Part6.BCLK
  N3: Part5.D0, Part6.LRCLK
  3.3V: Part5.3.3V, Part6.VIN

custom parts:
  Adafruit Metro M0 Express: Metro is our series of microcontroller boards for use with the Arduino IDE. This new Metro board looks a whole lot like our original Metro 328, but with a huge upgrade. Instead of the ATmega328, this Metro features a ATSAMD21G18 chip, an ARM Cortex M0+. It's our first Metro that is designed for use with CircuitPython! CircuitPython is our beginner-oriented flavor of MicroPython - and as the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
  Adafruit MAX98357A I2S 3W Class D Amplifier: Listen to this good news - we now have an all in one digital audio amp breakout board that works incredibly well with the Raspberry Pi! If you're looking for an easy and low cost way to get you digital sound files bumpin' then the MAX08357 I2S Amp Breakout is for you. It takes standard I2S digital audio input and, not only decodes it into analog, but also amplifies it directly into a speaker.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
