# Fritzing sketch MetroM4MAX98357 (saved by Fritzing 0.9.3b)
breadboards: 1

parts:
  Part1 = Adafruit Metro M4 Express [part_number="Adafruit #3382"]
  Part2 = Adafruit MAX98357A I2S 3W Class D Amplifier [part_number="Adafruit #3006"]

nets:
  GND: Part1.GND, Part2.GND
  N1: Part1.D9, Part2.LRCLK
  N2: Part1.D8, Part2.DIN
  N3: Part1.D3, Part2.BCLK
  3.3V: Part1.3.3V, Part2.VIN

custom parts:
  Adafruit Metro M4 Express: Are you ready? Really ready? Cause here comes the fastest, most powerful Metro ever. The Adafruit Metro M4 featuring the Microchip ATSAMD51. This Metro is like a bullet train, with it's 120MHz Cortex M4 with floating point support. Your code will zig and zag and zoom, and with a bunch of extra peripherals for support, this will for sure be your favorite new chipset. To start off our ATSAMD51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
  Adafruit MAX98357A I2S 3W Class D Amplifier: Listen to this good news - we now have an all in one digital audio amp breakout board that works incredibly well with the Raspberry Pi! If you're looking for an easy and low cost way to get you digital sound files bumpin' then the MAX08357 I2S Amp Breakout is for you. It takes standard I2S digital audio input and, not only decodes it into analog, but also amplifies it directly into a speaker.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
