# Fritzing sketch tpl5110_esp8266 (saved by Fritzing 0.9.3b)
breadboards: 1

parts:
  Part1 = Adafruit TPL5110 Power Timer [part_number="Adafruit #3435"]
  Part2 = Adafruit Feather HUZZAH ESP8266 [part_number="Adafruit #2821"]
  Part3 = Adafruit Micro USB Breakout [part_number="Adafruit #1833"]
  Part4 = 12 NeoPixel Ring [part_number=1643]
  C1 = Capacitor Polarized [package=panasonic_d]

nets:
  N1: Part1.VDD, Part3.VBUS
  GND: Part1.GND, Part2.GND, Part3.GND, Part4.GND, C1.-
  N2: Part1.PWROUT, Part2.VBUS, Part4.VDD, C1.+
  N3: Part1.DONE, Part2.GPIO5/SCL
  N4: Part2.GPIO4/SDA, Part4.IN

custom parts:
  Adafruit TPL5110 Power Timer: With some development boards, low power usage is an afterthought. Especially when price and usability is the main selling point. So what should you do when its time to turn around and make that project of yours run on a battery or solar? Sure you could try to hot-air that regulator off, or you could jerry-rig a relay. Or, use a 555? Ugh, the options aren't that great. The Adafruit TPL5110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
  Adafruit Feather HUZZAH ESP8266: his is the Adafruit Feather HUZZAH ESP8266 - our take on an 'all-in-one' ESP8266 WiFi development board with built in USB and battery charging. Its an ESP8266 WiFi module with all the extras you need, ready to rock! We have other boards in the Feather family, check'em out here. At the Feather HUZZAH's heart is an ESP8266 WiFi microcontroller clocked at 80 MHz and at 3.3V logic. This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
  Adafruit Micro USB Breakout: Simple but effective - this breakout board has a USB Micro-B connector, with all 5 pins broken out. Great for pairing with a microcontroller with USB support, or adding USB 5V power to a project. We use a micro-AB connector with through-hole shielding pads for an excellent strong connection - it won't rip off by accident! Comes with one fully assembled and tested micro B breakout PCB and a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
  12 NeoPixel Ring: 12 ultra bright smart LED NeoPixels are arranged in a circle with 1.5" (37mm) outer diameter. The rings are 'chainable' - connect the output pin of one to the input pin of another. Use only one microcontroller pin to control as many as you can chain together! Each LED is addressable as the driver chip is inside the LED. Each one has ~18mA constant current drive so the color will be very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
