# Fritzing sketch tpl_esp8266 (saved by Fritzing 0.9.3b)
breadboards: 1

parts:
  Part4 = 12 NeoPixel Ring [part_number=1643]
  Part5 = Adafruit Feather HUZZAH ESP8266 [part_number="Adafruit #2821"]
  Part6 = Adafruit TPL5111 Reset Enable Timer [part_number="Adafruit #3573"]

nets:
  N1: Part4.IN, Part5.GPIO4/SDA
  VDD: Part4.VDD, Part5.3.3V
  GND: Part4.GND, Part5.GND, Part6.GND
  N2: Part5.EN, Part6.ENOUT
  N3: Part5.VBUS, Part6.VDD
  N4: Part5.GPIO5/SCL, Part6.DONE

custom parts:
  12 NeoPixel Ring: 12 ultra bright smart LED NeoPixels are arranged in a circle with 1.5" (37mm) outer diameter. The rings are 'chainable' - connect the output pin of one to the input pin of another. Use only one microcontroller pin to control as many as you can chain together! Each LED is addressable as the driver chip is inside the LED. Each one has ~18mA constant current drive so the color will be very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
  Adafruit Feather HUZZAH ESP8266: his is the Adafruit Feather HUZZAH ESP8266 - our take on an 'all-in-one' ESP8266 WiFi development board with built in USB and battery charging. Its an ESP8266 WiFi module with all the extras you need, ready to rock! We have other boards in the Feather family, check'em out here. At the Feather HUZZAH's heart is an ESP8266 WiFi microcontroller clocked at 80 MHz and at 3.3V logic. This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
  Adafruit TPL5111 Reset Enable Timer: The Adafruit TPL5111 Reset Enable Timer is a stand-alone breakout that will turn any electronics into low-power electronics! It will take care of enabling & disabling your electronics using a built in timer that can vary from once-every 100ms up to once every two hours. Basically, the TPL will set an enable pin high periodically, adjustable by potentiometer or resistor, and turn on your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
