# Fritzing sketch FeatherM0UDA1334 (saved by Fritzing 0.9.3b)
breadboards: 1

parts:
  Part1 = Adafruit Feather M0 Express [part_number="Adafruit #3403"]
  Part2 = Adafruit UDA1334 I2S DAC [part_number="Adafruit #3678"]

nets:
  GND: Part1.GND, Part2.GND
  N1: Part1.TX, Part2.BITCLK_IN
  N2: Part1.RX, Part2.WORDSEL_IN
  +3V3: Part1.+3V3, Part2.VIN
  N3: Part1.D9, Part2.DATA_IN

custom parts:
  Adafruit Feather M0 Express: We love all our Feathers equally, but this Feather is very special. It's our first Feather that is specifically designed for use with CircuitPython! CircuitPython is our beginner-oriented flavor of MicroPython - and as the name hints at, its a small but full-featured version of the popular Python programming language specifically for use with circuitry and electronics. That doesn't mean you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
  Adafruit UDA1334 I2S DAC: This fully-featured UDA1334A I2S Stereo DAC breakout is a perfect match for any I2S-output audio interface. It's affordable but sounds great! The NXP UDA1334A is a jack-of-all-I2S-trades: you can use 3.3V - 5V logic levels (a rarity), and can process multiple different formats by setting two pins to high or low. The DAC will process data immediately, and give you a clear, analog, stereo line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
