# Fritzing sketch FeatherM4UDA1334 (saved by Fritzing 0.9.3b)
breadboards: 1

parts:
  Part1 = Adafruit Feather M4 Express [part_number="Adafruit #3857"]
  Part2 = Adafruit UDA1334 I2S DAC [part_number="Adafruit #3678"]

nets:
  N1: Part1.TX_D1, Part2.BITCLK_IN
  N2: Part1.A0, Part2.GND
  +3V3: Part1.+3V3, Part2.VIN
  N3: Part1.D11, Part2.DATA_IN
  N4: Part1.D10, Part2.WORDSEL_IN

custom parts:
  Adafruit Feather M4 Express: It's what you've been waiting for, the Feather M4 Express featuring ATSAMD51. This Feather is fast like a swift, smart like an owl, strong like a ox-bird (it's half ox, half bird, OK?) This feather is powered by our new favorite chip, the ATSAMD51J19 - with its 120MHz Cortex M4 with floating point support and 512KB Flash and 192KB RAM. Your code will zig and zag and zoom, and with a bunch of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
  Adafruit UDA1334 I2S DAC: This fully-featured UDA1334A I2S Stereo DAC breakout is a perfect match for any I2S-output audio interface. It's affordable but sounds great! The NXP UDA1334A is a jack-of-all-I2S-trades: you can use 3.3V - 5V logic levels (a rarity), and can process multiple different formats by setting two pins to high or low. The DAC will process data immediately, and give you a clear, analog, stereo line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
