# Fritzing sketch ItsyBitsyM0UDA1334 (saved by Fritzing 0.9.3b)
breadboards: 1

parts:
  Part1 = Itsy Bitsy M0 Express
  Part2 = Adafruit UDA1334 I2S DAC [part_number="Adafruit #3678"]

nets:
  GND: Part1.GND, Part2.GND
  N1: Part1.D9, Part2.DATA_IN
  N2: Part1.D1, Part2.BITCLK_IN
  N3: Part1.D0, Part2.WORDSEL_IN
  +3V3: Part1.+3V3, Part2.VIN

custom parts:
  Itsy Bitsy M0 Express: What's smaller than a Feather but larger than a Trinket? It's an Adafruit ItsyBitsy M0 Express! Small, powerful, with a rockin' ATSAMD21 Cortex M0 processor running at 48 MHz - this microcontroller board is perfect when you want something very compact, but still with a bunch of pins. ItsyBitsy M0 Express is only 1.4" long by 0.7" wide, but has 6 power pins, 23 digital GPIO pins (12 of which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
  Adafruit UDA1334 I2S DAC: This fully-featured UDA1334A I2S Stereo DAC breakout is a perfect match for any I2S-output audio interface. It's affordable but sounds great! The NXP UDA1334A is a jack-of-all-I2S-trades: you can use 3.3V - 5V logic levels (a rarity), and can process multiple different formats by setting two pins to high or low. The DAC will process data immediately, and give you a clear, analog, stereo line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
