# Fritzing sketch arduino uda (saved by Fritzing 0.9.3b)
breadboards: 1

parts:
  Part1 = Adafruit UDA1334 I2S DAC [part_number="Adafruit #3678"]
  Part2 = Adafruit Metro M0 Express

nets:
  VIN: Part1.VIN, Part2.3.3V
  GND: Part1.GND, Part2.GND
  N1: Part1.WORDSEL_IN, Part2.D0
  N2: Part1.DATA_IN, Part2.D9
  N3: Part1.OUTL, Part2.D1

custom parts:
  Adafruit UDA1334 I2S DAC: This fully-featured UDA1334A I2S Stereo DAC breakout is a perfect match for any I2S-output audio interface. It's affordable but sounds great! The NXP UDA1334A is a jack-of-all-I2S-trades: you can use 3.3V - 5V logic levels (a rarity), and can process multiple different formats by setting two pins to high or low. The DAC will process data immediately, and give you a clear, analog, stereo line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
  Adafruit Metro M0 Express: Metro is our series of microcontroller boards for use with the Arduino IDE. This new Metro board looks a whole lot like our original Metro 328, but with a huge upgrade. Instead of the ATmega328, this Metro features a ATSAMD21G18 chip, an ARM Cortex M0+. It's our first Metro that is designed for use with CircuitPython! CircuitPython is our beginner-oriented flavor of MicroPython - and as the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
