# Fritzing sketch piuda (saved by Fritzing 0.9.3b)
breadboards: 1

parts:
  Part1 = Adafruit UDA1334 I2S DAC [part_number="Adafruit #3678"]
  Part2 = Adafruit T-Cobbler Plus [part_number="Adafruit #1989 and #2028"]

nets:
  VIN: Part1.VIN, Part2.+3.3V
  GND: Part1.GND, Part2.GND
  N1: Part1.WORDSEL_IN, Part2.GPIO19
  N2: Part1.DATA_IN, Part2.GPIO21
  N3: Part1.BITCLK_IN, Part2.GPIO18

custom parts:
  Adafruit UDA1334 I2S DAC: This fully-featured UDA1334A I2S Stereo DAC breakout is a perfect match for any I2S-output audio interface. It's affordable but sounds great! The NXP UDA1334A is a jack-of-all-I2S-trades: you can use 3.3V - 5V logic levels (a rarity), and can process multiple different formats by setting two pins to high or low. The DAC will process data immediately, and give you a clear, analog, stereo line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
  Adafruit T-Cobbler Plus: The Raspberry Pi has landed on the Maker World like a 40-GPIO pinned, quad-USB ported, credit card sized bomb of DIY joy. And while you can use most of our great Model B accessories by hooking up our downgrade cable, its probably a good time to upgrade your set up and accessorize using all of the 40 pins. That's why we now carry the Assembled Adafruit Pi T-Cobbler Plus - Breakout + Cable for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
