# Fritzing sketch Analog_Inputs_for_Raspberry_Pi_Using_the_MCP3008-Pi-Cobbler (saved by Fritzing 0.9.3b)
breadboards: 1

parts:
  Part1 = Adafruit Pi Cobbler [part_number="Adafruit #914"]  # not connected
  IC1 = MCP3008 8-channel 10-bit ADC [part_number=MCP3008]
  POT1 = Breadboard Trimpot

nets:
  N1: IC1.no_name_yet#1, POT1.PIN2
  N2: IC1.no_name_yet#9, IC1.no_name_yet#14, POT1.PIN1
  N3: IC1.no_name_yet#15, IC1.no_name_yet#16, POT1.PIN3

custom parts:
  Adafruit Pi Cobbler: Now that you've finally got your hands on a Raspberry Pi® Model B , you're probably itching to make some fun embedded computer projects with it. What you need is an add on prototyping Pi Cobbler from Adafruit, which can break out all those tasty power, GPIO, I2C and SPI pins from the 26 pin header onto a solderless breadboard. This set will make "cobbling together" prototypes with the Pi super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
