# Fritzing sketch Analog_Inputs_for_Raspberry_Pi_Using_the_MCP3008-T-Cobbler-Plus (saved by Fritzing 0.9.3b)
breadboards: 1

parts:
  Part2 = Adafruit T-Cobbler Plus [part_number="Adafruit #1989 and #2028"]  # not connected
  IC1 = MCP3008 8-channel 10-bit ADC [part_number=MCP3008]
  POT1 = Breadboard Trimpot

nets:
  N1: IC1.no_name_yet#1, POT1.PIN2
  N2: IC1.no_name_yet#9, IC1.no_name_yet#14, POT1.PIN1
  N3: IC1.no_name_yet#15, IC1.no_name_yet#16, POT1.PIN3

custom parts:
  Adafruit T-Cobbler Plus: The Raspberry Pi has landed on the Maker World like a 40-GPIO pinned, quad-USB ported, credit card sized bomb of DIY joy. And while you can use most of our great Model B accessories by hooking up our downgrade cable, its probably a good time to upgrade your set up and accessorize using all of the 40 pins. That's why we now carry the Assembled Adafruit Pi T-Cobbler Plus - Breakout + Cable for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
