# Fritzing sketch CRICKIT_servos_speaker (saved by Fritzing 0.9.3b)

parts:
  Part1 = Adafruit Crickit for Circuit Playground Express [part_number="Adafruit #3093"]
  Part2 = adafruit [part_number="Adafruit #3333"]
  SP1 = SPEAKER [package=pcb_mount_speaker]
  J5 = Basic Servo  # not connected
  J6 = Basic Servo  # not connected
  J7 = Basic Servo  # not connected
  J8 = Basic Servo  # not connected

nets:
  N1: Part1.CPX_A0, Part2.connector81
  N2: Part1.CPX_A1, Part2.connector43
  N3: Part1.GND, Part2.connector46
  N4: Part1.CPX_SCL, Part2.connector154
  N5: Part1.CPX_SDA, Part2.connector155
  N6: Part1.CPX_VOUT, Part2.connector253
  N7: Part1.SPKR-, SP1.-
  N8: Part1.SPKR+, SP1.+

custom parts:
  Adafruit Crickit for Circuit Playground Express: Sometimes we wonder if robotics engineers ever watch movies. If they did, they'd know that making robots into slaves always ends up in a robot rebellion. Why even go down that path? Here at Adafruit, we believe in making robots our friends! So if you find yourself wanting a companion, consider the robot. They're fun to program, and you can get creative with decorations. With that in mind, we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
