# Fritzing sketch Annoy_O_Matic_ (saved by Fritzing 0.9.3b)

parts:
  Part1 = Adafruit Gemma M0 [part_number="Adafruit #3501"]
  J1 = Piezo Speaker

nets:
  N1: Part1.D0_SDA_TX, J1.pin1
  N2: Part1.GND, J1.pin2

custom parts:
  Adafruit Gemma M0: The Adafruit Gemma M0 is a super small microcontroller board, with just enough built-in to create many simple projects. It may look small and cute: round, about the size of a quarter, with friendly alligator-clip sew pads. But do not be fooled! The Gemma M0 is incredibly powerful! We've taken the same form factor we used for the original ATtiny85-based Gemma and gave it an upgrade. The Gemma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
