# Fritzing sketch astrophotography_mount (saved by Fritzing 0.9.4)
breadboards: 1

parts:
  part = Electrolytic Capacitor [capacitance=100µF voltage=16V package="100 mil [THT, electrolytic]"]
  Part2 = Adafruit Feather M0 Express [part_number="Adafruit #3403"]
  12V_power_supply = Stepper Motor - Bipolar
  Part3 = TSSOP20 [chip_label="TMC2226-BOB v1.1" package=TSSOP]

nets:
  N1: part.-, Part3.12, Part3.17
  N2: part.+, Part3.11
  N3: Part2.GND, Part3.5, Part3.9, Part3.18
  N4: Part2.+3V3, Part3.10, Part3.19
  N5: Part2.D6, Part3.2
  N6: Part2.D5, Part3.VCC
  N7: 12V_power_supply.A, Part3.16
  N8: 12V_power_supply.C, Part3.15
  N9: 12V_power_supply.B, Part3.14
  N10: 12V_power_supply.D, Part3.13

custom parts:
  Adafruit Feather M0 Express: We love all our Feathers equally, but this Feather is very special. It's our first Feather that is specifically designed for use with CircuitPython! CircuitPython is our beginner-oriented flavor of MicroPython - and as the name hints at, its a small but full-featured version of the popular Python programming language specifically for use with circuitry and electronics. That doesn't mean you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
