# Fritzing sketch AtariFruitJoystick (saved by Fritzing 0.9.3b)

parts:
  Part1 = Adafruit Micro USB Breakout [part_number="Adafruit #1833"]
  Part2 = Adafruit Feather nRF52 [part_number="Adafruit #3406"]
  S1 = Toggle Switch [package=THT]
  Part3 = Lithium Ion Polymer Battery 3.7v 500mAh [part_number=1578]  # not connected

nets:
  GND: Part1.GND, Part2.GND, S1.L1
  N1: Part1.VBUS, Part2.VBUS
  N2: Part2.EN, S1.COM

notes:
  Atari CX40

custom parts:
  Adafruit Micro USB Breakout: Simple but effective - this breakout board has a USB Micro-B connector, with all 5 pins broken out. Great for pairing with a microcontroller with USB support, or adding USB 5V power to a project. We use a micro-AB connector with through-hole shielding pads for an excellent strong connection - it won't rip off by accident! Comes with one fully assembled and tested micro B breakout PCB and a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
  Lithium Ion Polymer Battery 3.7v 500mAh: Lithium ion polymer (also known as 'lipo' or 'lipoly') batteries are thin, light and powerful. The output ranges from 4.2V when completely charged to 3.7V. This battery has a capacity of 500mAh for a total of about 1.9 Wh. The batteries come pre-attached with a genuine 2-pin JST-PH connector as shown and include the necessary protection circuitry.
