# Fritzing sketch Breath_Tester (saved by Fritzing 0.9.3b)

parts:
  Part1 = Adafruit Trinket M0 [part_number="Adafruit #3500"]
  Part2 = Adafruit SGP30 Gas Sensor

nets:
  GND: Part1.GND, Part2.GND
  3.3V: Part1.3.3V, Part2.VIN
  N1: Part1.D2_A1_PA09_SCL_MISO, Part2.SCL
  N2: Part1.D0_A4_PA08_SDA, Part2.SDA
