# Fritzing sketch Buzzing_Mindfulness_Bracelet (saved by Fritzing 0.9.3b)

parts:
  Part2 = GEMMA v2
  Q1 = TRANSISTOR_NPN [package=to-92-ammo]
  R1 = Resistor [tolerance=±5% resistance=220 package=THT]
  D1 = Rectifier Diode [part_number=1N4001 package="Melf DO-213 AB [SMD]"]
  U1 = Vibration Motor- ROB-08449 [package=vibe-motor-10mm]

nets:
  N1: Part2.B1, R1.Pin_0
  N2: Part2.GND, Q1.C
  N3: Part2.Vout, D1.cathode, U1.-
  N4: Q1.E, D1.anode, U1.+
  N5: Q1.B, R1.Pin_1

custom parts:
  GEMMA v2: Love FLORA but want a bite-sized version? Look no further, GEMMA is a tiny wearable platform board with a lot of might in a 1" diameter package. Powered by a Attiny85 and programmable with an Arduino IDE over USB, you'll be able to realize any wearable project! We wanted to design a microcontroller board that was small enough to fit into any project, and low cost enough to use without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
