# Fritzing sketch 5pad-sensor-wiring-40-pin (saved by Fritzing 0.9.3b)
breadboards: 1

parts:
  Part1 = Adafruit T-Cobbler Plus [part_number="Adafruit #1989 and #2028"]
  Part2 = Adafruit Standalone 5-Pad Capacitive Touch Sensor Breakout - AT42QT1070 [part_number="Adafruit #1362"]

nets:
  +3.3V: Part1.+3.3V, Part2.VDD
  N1: Part1.GPIO17, Part2.OUT2
  N2: Part1.GPIO22, Part2.OUT0
  N3: Part1.GPIO23, Part2.OUT4
  N4: Part1.GPIO24, Part2.OUT3
  N5: Part1.GPIO21, Part2.OUT1

notes:
  To Apples (optional)

custom parts:
  Adafruit T-Cobbler Plus: The Raspberry Pi has landed on the Maker World like a 40-GPIO pinned, quad-USB ported, credit card sized bomb of DIY joy. And while you can use most of our great Model B accessories by hooking up our downgrade cable, its probably a good time to upgrade your set up and accessorize using all of the 40 pins. That's why we now carry the Assembled Adafruit Pi T-Cobbler Plus - Breakout + Cable for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
  Adafruit Standalone 5-Pad Capacitive Touch Sensor Breakout - AT42QT1070: This breakout board is the simplest way to create a project with mutiple capacitive touch sensors. No microcontroller is required here - just power with 1.8 to 5.5VDC and connect up to 5 conductive pads to the 5 left-hand pins. When a capacitive load is detected (e.g. a person touches one of the conductive contacts) the corresponding LED on the right lights up and the output pin goes low. You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
