# Fritzing sketch toggle-board-wiring-40-pin (saved by Fritzing 0.9.3b)
breadboards: 1

parts:
  Part1 = Adafruit T-Cobbler Plus [part_number="Adafruit #1989 and #2028"]
  R1 = Resistor [tolerance=±5% resistance=10k package="0402 [SMD]"]
  Part2 = Adafruit AT42QT1012 Standalone Toggle Capacitive Touch Sensor Breakout [part_number="Adafruit #1375"]

nets:
  +3.3V: Part1.+3.3V, Part2.VDD
  GND: Part1.GND, R1.Pin_0, Part2.GND
  N1: Part1.GPIO23, R1.Pin_1, Part2.OUT

custom parts:
  Adafruit T-Cobbler Plus: The Raspberry Pi has landed on the Maker World like a 40-GPIO pinned, quad-USB ported, credit card sized bomb of DIY joy. And while you can use most of our great Model B accessories by hooking up our downgrade cable, its probably a good time to upgrade your set up and accessorize using all of the 40 pins. That's why we now carry the Assembled Adafruit Pi T-Cobbler Plus - Breakout + Cable for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
  Adafruit AT42QT1012 Standalone Toggle Capacitive Touch Sensor Breakout: This breakout board is the simplest way to create a project with a single "toggle" capacitive touch sensor. No microcontroller is required here - just power with 1.8 to 5.5VDC and touch the pad to activate the sensor. This sensor is a toggle output type: touch-on then touch-off. That means that when a capacitive load is detected (e.g. a person touches the sensor-pad area) the red LED will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
