# Fritzing sketch m0_charlcd (saved by Fritzing 0.9.3b)
breadboards: 1

parts:
  Part1 = Adafruit Metro M0 Express
  POT1 = Breadboard Trimpot
  U1 = LCD-16X2 [package=lcd-16x2]

nets:
  GND: Part1.GND, POT1.PIN1, U1.VSS, U1.R_W, U1.K
  N1: Part1.D12, U1.DB7
  N2: Part1.D11, U1.DB6
  N3: Part1.D10, U1.DB5
  N4: Part1.D9, U1.DB4
  N5: Part1.D8, U1.E
  N6: Part1.D7, U1.RS
  +5V: Part1.+5V, POT1.PIN3, U1.VDD, U1.A
  N7: POT1.PIN2, U1.VO

custom parts:
  Adafruit Metro M0 Express: Metro is our series of microcontroller boards for use with the Arduino IDE. This new Metro board looks a whole lot like our original Metro 328, but with a huge upgrade. Instead of the ATmega328, this Metro features a ATSAMD21G18 chip, an ARM Cortex M0+. It's our first Metro that is designed for use with CircuitPython! CircuitPython is our beginner-oriented flavor of MicroPython - and as the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
