# Fritzing sketch m0_charlcd_rgb (saved by Fritzing 0.9.3b)
breadboards: 1

parts:
  Part1 = Adafruit Metro M0 Express
  POT1 = Breadboard Trimpot
  LCD1 = Adafruit Positive RGB 2x16 LCD

nets:
  N1: Part1.+5V, POT1.PIN3, LCD1.no_name_yet#1, LCD1.no_name_yet#14
  N2: Part1.GND, POT1.PIN1, LCD1.no_name_yet#0, LCD1.no_name_yet#4
  N3: Part1.D12, LCD1.no_name_yet#13
  N4: Part1.D11, LCD1.no_name_yet#12
  N5: Part1.D10, LCD1.no_name_yet#11
  N6: Part1.D9, LCD1.no_name_yet#10
  N7: Part1.D8, LCD1.no_name_yet#5
  N8: Part1.D7, LCD1.no_name_yet#3
  N9: Part1.D6, LCD1.no_name_yet#17
  N10: Part1.D5, LCD1.no_name_yet#16
  N11: Part1.D3, LCD1.no_name_yet#15
  N12: POT1.PIN2, LCD1.no_name_yet#2

custom parts:
  Adafruit Metro M0 Express: Metro is our series of microcontroller boards for use with the Arduino IDE. This new Metro board looks a whole lot like our original Metro 328, but with a huge upgrade. Instead of the ATmega328, this Metro features a ATSAMD21G18 chip, an ARM Cortex M0+. It's our first Metro that is designed for use with CircuitPython! CircuitPython is our beginner-oriented flavor of MicroPython - and as the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
  Adafruit Positive RGB 2x16 LCD: Adafruit Positive 2x16 LCD Display with RGB Backlight
