# Fritzing sketch Circadian_Pi_Desk_Light (saved by Fritzing 0.9.3b)
breadboards: 1

parts:
  Part1 = Adafruit Pi Cobbler Plus [part_number="Adafruit #2029"]
  NEOPIXEL1 = Neopixel Strip -- Black (30/m) [part_number=1376]
  JACK1 = 2.1mm Barrel Jack with Terminal Block

nets:
  GND: Part1.GND, NEOPIXEL1.GND, JACK1.NEG
  N1: Part1.GPIO18, NEOPIXEL1.Din
  N2: NEOPIXEL1.+5V, JACK1.POS

custom parts:
  Adafruit Pi Cobbler Plus: The Raspberry Pi B+/Pi 2/ Pi 3 has landed on the Maker World like a 40-GPIO pinned, quad-USB ported, credit card sized bomb of DIY joy. And while you can use most of our great Model B accessories by hooking up our downgrade cable, its probably a good time to upgrade your set up and accessorize using all of the Model B+'s / Pi 2's / Pi 3's 40 pins. That's why we now carry the Adafruit Assembled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
  Neopixel Strip -- Black (30/m): These NeoPixel strips have 30 digitally-addressable pixel LEDs per meter and are very affordable and are only 12.5 mm wide, 10 mm if you remove the strip from the casing.
