# Fritzing sketch Wiring (saved by Fritzing 0.9.0b)

parts:
  U2 = HC-SR04 [chip_label=IC package="SIP (Single Inline) [THT]"]
  Part1 = Adafruit Crickit for micro:bit [part_number=3928]
  M1 = DC Motor
  M2 = DC Motor
  SP1 = SPEAKER [package=pcb_mount_speaker]

nets:
  N1: U2.Vcc, Part1.5.0V
  N2: U2.Trig, Part1.#8
  N3: U2.Echo, Part1.#2
  GND: U2.GND, Part1.GND
  N4: Part1.MOTOR_2B_OUT, M1.pin_1
  N5: Part1.MOTOR_2A_OUT, M1.pin_2
  N6: Part1.MOTOR_1B_OUT, M2.pin_2
  N7: Part1.MOTOR_1A_OUT, M2.pin_1
  N8: Part1.SPKR-, SP1.+
  N9: Part1.SPKR+, SP1.-

custom parts:
  HC-SR04: HC-SR04 ultrasound distance sensor
  Adafruit Crickit for micro:bit: Crickit is our Creative Robotics & Interactive Construction Kit. It's an add-on to the BBC micro:bit that lets you #MakeRobotFriend using MicroPython. Plug your micro:bit into the socket and start controlling motors, servos, solenoids. You also get signal pins, capacitive touch sensors, a NeoPixel driver and amplified speaker output. It complements & extends the micro:bit so you can still use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
