# Fritzing sketch dont_fear_the_crickit (saved by Fritzing 0.9.3b)

parts:
  Part1 = Adafruit Crickit for Circuit Playground Express [part_number="Adafruit #3093"]
  J1 = Basic Servo
  J2 = Basic Servo
  U2 = POT [package=alps_pot]
  U3 = SWITCH-SPST-2 [package=switch-spst-vertical]
  SP1 = SPEAKER [package=pcb_mount_speaker]
  NEOPIXEL1 = Neopixel Strip -- White (30/m)
  U4 = mystery part, 4 pins [chip_label="Fog Radio"]
  Part2 = Adafruit Circuit Playground Express [part_number="Adafruit #3333"]

nets:
  N1: Part1.CPX_A0, Part2.D12_A0_SPEAKER
  N2: Part1.CPX_A1, Part2.D6_A1
  GND: Part1.GND, J1.gnd, J2.gnd, U2.A, U3.P, NEOPIXEL1.GND, U4.pin4, Part2.GND
  N3: Part1.CPX_SCL, Part2.D3_A4_SCL
  N4: Part1.CPX_SDA, Part2.D2_A5_SDA
  N5: Part1.CPX_VOUT, Part2.VOUT
  N6: Part1.ANALOG1, U2.S
  N7: Part1.3.3V, U2.E
  N8: Part1.ANALOG2, U3.O
  VCC: Part1.5.0V, J1.vcc, J2.vcc, NEOPIXEL1.+5V, U4.pin1
  N9: Part1.MOTOR_1B_OUT, U4.pin3
  N10: Part1.MOTOR_1A_OUT, U4.pin2
  N11: Part1.NEOPIXELOUT, NEOPIXEL1.Din
  N12: Part1.SERVO1, J1.pulse
  N13: Part1.SERVO2, J2.pulse
  N14: Part1.SPKR-, SP1.-
  N15: Part1.SPKR+, SP1.+

notes:
  Fog Machine Remote:
  5V to Battery +
  GND to Battery -
  Motor 1A to Button 1
  Motor 1B to Button 2

custom parts:
  Adafruit Crickit for Circuit Playground Express: Sometimes we wonder if robotics engineers ever watch movies. If they did, they'd know that making robots into slaves always ends up in a robot rebellion. Why even go down that path? Here at Adafruit, we believe in making robots our friends! So if you find yourself wanting a companion, consider the robot. They're fun to program, and you can get creative with decorations. With that in mind, we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
  Neopixel Strip -- White (30/m): These NeoPixel strips have 30 digitally-addressable pixel LEDs per meter and are very affordable and are only 12.5 mm wide, 10 mm if you remove the strip from the casing.
  Adafruit Circuit Playground Express: Circuit Playground Express is the next step towards a perfect introduction to electronics and programming. We've taken the original Circuit Playground Classic and made it even better! Not only did we pack even more sensors in, we also made it even easier to program. You can now start your journey with Microsoft MakeCode block-based or Javascript programming. Then, you can use the same board to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
