# Fritzing sketch ghosty (saved by Fritzing 0.9.3b)

parts:
  Part1 = Adafruit Crickit for Circuit Playground Express [part_number="Adafruit #3093"]
  Part2 = Adafruit Circuit Playground Express [part_number="Adafruit #3333"]
  SP1 = SPEAKER [package=pcb_mount_speaker]
  M1 = DC Motor
  NEOPIXEL1 = Neopixel Strip -- White (30/m)
  U2 = POT [package=pot_alpha_rv16af-20]
  R1 = Resistor [tolerance=±5% resistance=10k package="2512 [SMD]"]

nets:
  N1: Part1.CPX_A0, Part2.D12_A0_SPEAKER
  N2: Part1.CPX_A1, Part2.D6_A1
  GND: Part1.GND, Part2.GND, NEOPIXEL1.GND, U2.E
  N3: Part1.CPX_SCL, Part2.D3_A4_SCL
  N4: Part1.CPX_SDA, Part2.D2_A5_SDA
  N5: Part1.CPX_VOUT, Part2.VOUT
  N6: Part1.ANALOG1, U2.S, R1.Pin_0
  N7: Part1.3.3V, R1.Pin_1
  N8: Part1.MOTOR_1B_OUT, M1.pin_2
  N9: Part1.MOTOR_1A_OUT, M1.pin_1
  N10: Part1.5.0V, NEOPIXEL1.+5V
  N11: Part1.NEOPIXELOUT, NEOPIXEL1.Din
  N12: Part1.SPKR-, SP1.-
  N13: Part1.SPKR+, SP1.+

notes:
  Foot switch is like half of a 20K potentiometer
  Then a 10K resistor is a pullup to 3.3V for the other half

custom parts:
  Adafruit Crickit for Circuit Playground Express: Sometimes we wonder if robotics engineers ever watch movies. If they did, they'd know that making robots into slaves always ends up in a robot rebellion. Why even go down that path? Here at Adafruit, we believe in making robots our friends! So if you find yourself wanting a companion, consider the robot. They're fun to program, and you can get creative with decorations. With that in mind, we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
  Adafruit Circuit Playground Express: Circuit Playground Express is the next step towards a perfect introduction to electronics and programming. We've taken the original Circuit Playground Classic and made it even better! Not only did we pack even more sensors in, we also made it even easier to program. You can now start your journey with Microsoft MakeCode block-based or Javascript programming. Then, you can use the same board to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
  Neopixel Strip -- White (30/m): These NeoPixel strips have 30 digitally-addressable pixel LEDs per meter and are very affordable and are only 12.5 mm wide, 10 mm if you remove the strip from the casing.
