# Fritzing sketch Cyberpunk_Spikes (saved by Fritzing 0.9.3b)

parts:
  Part1 = GEMMA v2
  NEOPIXEL1 = Neopixel Strip -- Black (30/m)

nets:
  N1: Part1.B1, NEOPIXEL1.Din
  GND: Part1.GND, NEOPIXEL1.GND
  N2: Part1.Vout, NEOPIXEL1.+5V

custom parts:
  GEMMA v2: Love FLORA but want a bite-sized version? Look no further, GEMMA is a tiny wearable platform board with a lot of might in a 1" diameter package. Powered by a Attiny85 and programmable with an Arduino IDE over USB, you'll be able to realize any wearable project! We wanted to design a microcontroller board that was small enough to fit into any project, and low cost enough to use without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
  Neopixel Strip -- Black (30/m): These NeoPixel strips have 30 digitally-addressable pixel LEDs per meter and are very affordable and are only 12.5 mm wide, 10 mm if you remove the strip from the casing.
