# Fritzing sketch Cobbler-v1-Drive_a_16x2_LCD_with_the_Raspberry_Pi (saved by Fritzing 0.9.3b)
breadboards: 2

parts:
  U1 = LCD-16X2 [package=lcd-16x2_noholes]
  Part1 = Adafruit Pi Cobbler [part_number="Adafruit #914"]
  POT1 = Breadboard Trimpot

nets:
  VSS: U1.VSS, U1.R_W, U1.K, Part1.GND, POT1.PIN1
  N1: U1.VDD, U1.A, Part1.5.0V, POT1.PIN3
  N2: U1.VO, POT1.PIN2
  N3: U1.RS, Part1.GPIO22
  N4: U1.E, Part1.GPIO17
  N5: U1.DB4, Part1.GPIO25
  N6: U1.DB5, Part1.GPIO24
  N7: U1.DB6, Part1.GPIO23
  N8: U1.DB7, Part1.GPIO18

custom parts:
  Adafruit Pi Cobbler: Now that you've finally got your hands on a Raspberry Pi® Model B , you're probably itching to make some fun embedded computer projects with it. What you need is an add on prototyping Pi Cobbler from Adafruit, which can break out all those tasty power, GPIO, I2C and SPI pins from the 26 pin header onto a solderless breadboard. This set will make "cobbling together" prototypes with the Pi super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
