# Fritzing sketch T-Cobbler-Plus-Drive_a_16x2_LCD_with_the_Raspberry_Pi (saved by Fritzing 0.9.3b)
breadboards: 2

parts:
  U1 = LCD-16X2 [package=lcd-16x2_noholes]
  POT1 = Breadboard Trimpot
  Part2 = Adafruit T-Cobbler Plus [part_number="Adafruit #1989 and #2028"]

nets:
  VSS: U1.VSS, U1.R_W, U1.K, POT1.PIN1, Part2.GND
  VDD: U1.VDD, U1.A, POT1.PIN3, Part2.+5V
  N1: U1.VO, POT1.PIN2
  N2: U1.RS, Part2.GPIO22
  N3: U1.E, Part2.GPIO17
  N4: U1.DB4, Part2.GPIO25
  N5: U1.DB5, Part2.GPIO24
  N6: U1.DB6, Part2.GPIO23
  N7: U1.DB7, Part2.GPIO18

custom parts:
  Adafruit T-Cobbler Plus: The Raspberry Pi has landed on the Maker World like a 40-GPIO pinned, quad-USB ported, credit card sized bomb of DIY joy. And while you can use most of our great Model B accessories by hooking up our downgrade cable, its probably a good time to upgrade your set up and accessorize using all of the 40 pins. That's why we now carry the Assembled Adafruit Pi T-Cobbler Plus - Breakout + Cable for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
