# Fritzing sketch Servo_RecordPlay_Feather_M4_Express (saved by Fritzing 0.9.3b)
breadboards: 1

parts:
  Part1 = Adafruit Feather M0 Express [part_number="Adafruit #3403"]
  LED3 = LED - 5mm [color="Red (633nm)" package="5 mm [THT]"]
  R1 = Resistor [tolerance=±5% resistance=220 package="0805 [SMD]"]
  S1 = Momentary Switch [package=ksa_sealed_tac_switch]
  S2 = Momentary Switch [package=ksa_sealed_tac_switch]
  J1 = Basic Servo

nets:
  GND: Part1.GND, R1.Pin_0, S1.2, S2.2, J1.gnd
  N1: Part1.A1, J1.pulse
  N2: Part1.VBUS, J1.vcc
  N3: Part1.D13, LED3.anode
  N4: Part1.D10, S1.3
  N5: Part1.D9, S2.3
  N6: LED3.cathode, R1.Pin_1

custom parts:
  Adafruit Feather M0 Express: We love all our Feathers equally, but this Feather is very special. It's our first Feather that is specifically designed for use with CircuitPython! CircuitPython is our beginner-oriented flavor of MicroPython - and as the name hints at, its a small but full-featured version of the popular Python programming language specifically for use with circuitry and electronics. That doesn't mean you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
