# Fritzing sketch Servo_RecordPlay_Feather_RP2040 (saved by Fritzing 0.9.5d)
breadboards: 1

parts:
  J1 = Basic Servo
  LED1 = smd LED [color="Red (633nm)" package="0805 [SMD]"]
  R1 = Resistor [tolerance=±5% resistance=220 package=THT]
  S1 = Pushbutton [package="[THT]"]
  S2 = Pushbutton [package="[THT]"]
  Part1 = Adafruit Feather RP2040 [part_number="Adafruit #4884"]

nets:
  GND: J1.gnd, R1.Pin_1, S1.Pin_1, S1.Pin_2, S2.Pin_1, S2.Pin_2, Part1.GND
  N1: J1.vcc, Part1.VBUS
  N2: J1.pulse, Part1.A1
  N3: LED1.cathode, R1.Pin_0
  N4: LED1.anode, Part1.D13
  N5: S1.Pin_3, S1.Pin_4, Part1.D10
  N6: S2.Pin_3, S2.Pin_4, Part1.D9

custom parts:
  Adafruit Feather RP2040: A new chip means a new Feather, and the Raspberry Pi RP2040 is no exception. When we saw this chip we thought "this chip is going to be awesome when we give it the Feather Treatment" and so we did! This Feather features the RP2040, and all niceties you know and love about Feather Measures 2.0" x 0.9" x 0.28" (50.8mm x 22.8mm x 7mm) without headers soldered in Light as a (large?) feather - 5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
