# Fritzing sketch fruitSpeaker (saved by Fritzing 0.9.3b)

parts:
  Part1 = Adafruit Circuit Playground Express [part_number="Adafruit #3333"]  # not connected
  C1 = Electrolytic Capacitor [capacitance=1µF package="100 mil [THT, electrolytic]"]  # not connected
  CLIP1 = Alligator Clip
  CLIP2 = Alligator Clip
  CLIP3 = Alligator Clip
  CLIP4 = Alligator Clip
  SP1 = SPEAKER [package=pcb_mount_speaker]  # not connected
  CLIP5 = Alligator Clip
  CLIP6 = Alligator Clip

nets:
  N1: CLIP1.wire, CLIP2.wire
  N2: CLIP3.wire, CLIP4.wire
  N3: CLIP5.wire, CLIP6.wire

custom parts:
  Adafruit Circuit Playground Express: Circuit Playground Express is the next step towards a perfect introduction to electronics and programming. We've taken the original Circuit Playground Classic and made it even better! Not only did we pack even more sensors in, we also made it even easier to program. You can now start your journey with Microsoft MakeCode block-based or Javascript programming. Then, you can use the same board to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
  Alligator Clip: Alligator clip
  Alligator Clip: Alligator clip
  Alligator Clip: Alligator clip
  Alligator Clip: Alligator clip
