# Fritzing sketch Trinket_Gemma_M0_IR_Control (saved by Fritzing 0.9.3b)
breadboards: 1

parts:
  IR1 = TSOP312.., 314.. [package=THT]
  Part1 = GEMMA v2
  J1 = Piezo Speaker

nets:
  N1: IR1.GND, Part1.B2
  N2: IR1.Vs, Part1.GND, J1.pin1
  N3: IR1.Data, Part1.Vout
  N4: Part1.B0, J1.pin2

custom parts:
  GEMMA v2: Love FLORA but want a bite-sized version? Look no further, GEMMA is a tiny wearable platform board with a lot of might in a 1" diameter package. Powered by a Attiny85 and programmable with an Arduino IDE over USB, you'll be able to realize any wearable project! We wanted to design a microcontroller board that was small enough to fit into any project, and low cost enough to use without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
