# Fritzing sketch GemmaM0_TV_B_GONE (saved by Fritzing 0.9.3b)

parts:
  Q1 = TRANSISTOR_NPN [package=to-92-ammo]
  Part1 = Adafruit Gemma M0 [part_number="Adafruit #3501"]
  LED1 = LED - 5mm [color="Infrared (940nm)" package="5 mm [THT]"]

nets:
  N1: Q1.E, Part1.GND
  N2: Q1.B, Part1.D0_SDA_TX
  N3: Part1.VOUT, LED1.anode

custom parts:
  Adafruit Gemma M0: The Adafruit Gemma M0 is a super small microcontroller board, with just enough built-in to create many simple projects. It may look small and cute: round, about the size of a quarter, with friendly alligator-clip sew pads. But do not be fooled! The Gemma M0 is incredibly powerful! We've taken the same form factor we used for the original ATtiny85-based Gemma and gave it an upgrade. The Gemma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
