# Fritzing sketch Gemma_Firewalker_Lite_Sneakers (saved by Fritzing 0.9.3b)

parts:
  Part1 = GEMMA v2
  S2 = Tilt Switch [package=THT]
  NEOPIXEL1 = Neopixel Strip -- White (60/m)
  U1 = LIPO-110mAh [package=lipo-110]  # not connected
  LED1 = prefix0000
  LED2 = prefix0000
  NEOPIXEL2 = Neopixel Strip -- White (60/m)

nets:
  N1: Part1.B0, S2.Pin_1
  N2: Part1.B1, NEOPIXEL1.DI
  N3: Part1.GND, S2.Pin_2, NEOPIXEL1.GND#3
  N4: Part1.Vout, NEOPIXEL1.+5V#1
  N5: NEOPIXEL1.GND#4, LED1.connector3, LED2.connector3, NEOPIXEL2.GND
  N6: NEOPIXEL1.DO, LED1.connector2
  N7: NEOPIXEL1.+5V#6, LED1.connector1, LED2.connector1, NEOPIXEL2.+5V
  N8: LED1.connector4, LED2.connector2
  N9: LED2.connector4, NEOPIXEL2.DI

custom parts:
  GEMMA v2: Love FLORA but want a bite-sized version? Look no further, GEMMA is a tiny wearable platform board with a lot of might in a 1" diameter package. Powered by a Attiny85 and programmable with an Arduino IDE over USB, you'll be able to realize any wearable project! We wanted to design a microcontroller board that was small enough to fit into any project, and low cost enough to use without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
  Neopixel Strip -- White (60/m): Neopixel Strip, White, 60 pixels per meter.
