# Fritzing sketch arduino-wiring (saved by Fritzing 0.9.3b)
breadboards: 1

parts:
  NEOPIXEL2 = Neopixel Strip -- Black (60/m) [part_number=1461]
  Part1 = Adafruit Feather HUZZAH ESP8266 [part_number="Adafruit #2821"]
  Part2 = NeoPixel Jewel [part_number=2226]
  Part3 = Adafruit Si7021 Temp Humidity [part_number="Adafruit #3251"]
  J1 = JST-03JQ-BT [part_number=JST-JQ-BT package=THT]
  J4 = JST-VHR-3N [part_number=JST-VHR-3N package=THT]

nets:
  N1: NEOPIXEL2.+5V, J1.pin1
  N2: NEOPIXEL2.DI, J1.pin2
  N3: NEOPIXEL2.GND, J1.pin3
  GND: Part1.GND, Part2.GND, Part3.GND, J4.pin3, J4.pin_6
  3.3V: Part1.3.3V, Part2.VDD, Part3.VIN, J4.pin1, J4.pin_4
  N4: Part1.GPIO16, Part2.IN
  N5: Part1.GPIO2, J4.pin2, J4.pin_5
  N6: Part1.GPIO5/SCL, Part3.SCL
  N7: Part1.GPIO4/SDA, Part3.SDA

custom parts:
  Neopixel Strip -- Black (60/m): Neopixel Strip, Black, 60 pixels per meter.
  Adafruit Feather HUZZAH ESP8266: his is the Adafruit Feather HUZZAH ESP8266 - our take on an 'all-in-one' ESP8266 WiFi development board with built in USB and battery charging. Its an ESP8266 WiFi module with all the extras you need, ready to rock! We have other boards in the Feather family, check'em out here. At the Feather HUZZAH's heart is an ESP8266 WiFi microcontroller clocked at 80 MHz and at 3.3V logic. This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
  NeoPixel Jewel: We fit seven of our tiny 5050 (5mm x 5mm) smart RGB LEDs onto a beautiful, round PCB with mounting holes and a chainable design to create what we think is our most elegant (and evening-wear appropriate) NeoPixel board yet. Use only one microcontroller pin to control as many as you can chain together! Each LED is addressable as the driver chip is inside the LED. Each one has ~18mA constant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
  Adafruit Si7021 Temp Humidity: It's summer and you're sweating and your hair's all frizzy and all you really want to know is why the weatherman said this morning that today's relative humidity would max out at a perfectly reasonable 42% when it feels more like 77%. Enter the Si7021 Temperature + Humidity Sensor - the best way to prove the weatherman wrong! This lovely sensor for Silicon labs has ± 3% relative humidity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
