# Fritzing sketch python-wiring (saved by Fritzing 0.9.3b)
breadboards: 1

parts:
  Part2 = Adafruit Si7021 Temp Humidity [part_number="Adafruit #3251"]
  J1 = JST-VHR-3N [part_number=JST-VHR-3N package=THT]
  J2 = JST-B3P-VH [part_number=JST-B3P-VH package=THT]
  NEOPIXEL1 = Neopixel Strip -- Black (60/m) [part_number=1461]
  Part3 = NeoPixel Jewel [part_number=2226]

nets:
  GND: Part2.GND, J2.pin1, Part3.GND
  N1: J1.pin_5, NEOPIXEL1.DI
  N2: J1.pin_4, NEOPIXEL1.GND
  N3: J1.pin_6, NEOPIXEL1.+5V
  N4: J2.pin2, Part3.OUT
  N5: J2.pin3, Part3.VDD

custom parts:
  Adafruit Si7021 Temp Humidity: It's summer and you're sweating and your hair's all frizzy and all you really want to know is why the weatherman said this morning that today's relative humidity would max out at a perfectly reasonable 42% when it feels more like 77%. Enter the Si7021 Temperature + Humidity Sensor - the best way to prove the weatherman wrong! This lovely sensor for Silicon labs has ± 3% relative humidity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
  Neopixel Strip -- Black (60/m): Neopixel Strip, Black, 60 pixels per meter.
  NeoPixel Jewel: We fit seven of our tiny 5050 (5mm x 5mm) smart RGB LEDs onto a beautiful, round PCB with mounting holes and a chainable design to create what we think is our most elegant (and evening-wear appropriate) NeoPixel board yet. Use only one microcontroller pin to control as many as you can chain together! Each LED is addressable as the driver chip is inside the LED. Each one has ~18mA constant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
