# Fritzing sketch arduino-wiring (saved by Fritzing 0.9.3b)
breadboards: 1

parts:
  NEOPIXEL2 = Neopixel Strip -- Black (60/m) [part_number=1461]
  Part1 = Adafruit Feather HUZZAH ESP8266 [part_number="Adafruit #2821"]
  J1 = JST-03JQ-BT [part_number=JST-JQ-BT package=THT]
  J4 = JST-VHR-3N [part_number=JST-VHR-3N package=THT]
  Part3 = Adafruit SGP30 Gas Sensor
  J5 = Piezo Speaker
  S3 = Reed switch [package=THT]
  PIR1 = PIR sensor
  Part2 = NeoPixel Jewel [part_number=2226]

nets:
  N1: NEOPIXEL2.+5V, J1.pin1
  N2: NEOPIXEL2.DI, J1.pin2
  N3: NEOPIXEL2.GND, J1.pin3
  N4: Part1.GPIO12/MISO, Part2.IN
  N5: Part1.GPIO13/MOSI, PIR1.SIG
  N6: Part1.GPIO14/SCK, J5.pin2
  GND: Part1.GND, J4.pin3, J4.pin_6, Part3.GND, J5.pin1, S3.pin_1, PIR1.GND, Part2.GND
  3.3V: Part1.3.3V, J4.pin1, J4.pin_4, Part3.VIN, Part2.VDD
  N7: Part1.VBUS, PIR1.VDD
  N8: Part1.GPIO2, S3.pin_2
  N9: Part1.GPIO5/SCL, Part3.SCL
  N10: Part1.GPIO4/SDA, Part3.SDA
  N11: J4.pin2, J4.pin_5, Part2.OUT

custom parts:
  Neopixel Strip -- Black (60/m): Neopixel Strip, Black, 60 pixels per meter.
  Adafruit Feather HUZZAH ESP8266: his is the Adafruit Feather HUZZAH ESP8266 - our take on an 'all-in-one' ESP8266 WiFi development board with built in USB and battery charging. Its an ESP8266 WiFi module with all the extras you need, ready to rock! We have other boards in the Feather family, check'em out here. At the Feather HUZZAH's heart is an ESP8266 WiFi microcontroller clocked at 80 MHz and at 3.3V logic. This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
  NeoPixel Jewel: We fit seven of our tiny 5050 (5mm x 5mm) smart RGB LEDs onto a beautiful, round PCB with mounting holes and a chainable design to create what we think is our most elegant (and evening-wear appropriate) NeoPixel board yet. Use only one microcontroller pin to control as many as you can chain together! Each LED is addressable as the driver chip is inside the LED. Each one has ~18mA constant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
