# Fritzing sketch play808 (saved by Fritzing 0.9.3b)

parts:
  Part2 = Adafruit Circuit Playground Express [part_number="Adafruit #3333"]  # not connected
  CLIP10 = Alligator Clip
  CLIP7 = Alligator Clip
  CLIP8 = Alligator Clip
  CLIP9 = Alligator Clip
  CLIP11 = Alligator Clip
  CLIP13 = Alligator Clip
  CLIP12 = Alligator Clip
  CLIP14 = Alligator Clip
  CLIP15 = Alligator Clip
  CLIP16 = Alligator Clip
  CLIP17 = Alligator Clip
  CLIP18 = Alligator Clip
  CLIP19 = Alligator Clip
  CLIP20 = Alligator Clip

nets:
  N1: CLIP10.wire, CLIP20.wire
  N2: CLIP7.wire, CLIP14.wire
  N3: CLIP8.wire, CLIP18.wire
  N4: CLIP9.wire, CLIP19.wire
  N5: CLIP11.wire, CLIP16.wire
  N6: CLIP13.wire, CLIP15.wire
  N7: CLIP12.wire, CLIP17.wire

custom parts:
  Adafruit Circuit Playground Express: Circuit Playground Express is the next step towards a perfect introduction to electronics and programming. We've taken the original Circuit Playground Classic and made it even better! Not only did we pack even more sensors in, we also made it even easier to program. You can now start your journey with Microsoft MakeCode block-based or Javascript programming. Then, you can use the same board to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
  Alligator Clip: Alligator clip
  Alligator Clip: Alligator clip
  Alligator Clip: Alligator clip
  Alligator Clip: Alligator clip
  Alligator Clip: Alligator clip
  Alligator Clip: Alligator clip
