# Fritzing sketch Jewel_Hair_Stick (saved by Fritzing 0.9.3b)

parts:
  Part1 = GEMMA v2
  Part2 = NeoPixel Jewel [part_number=2226]

nets:
  N1: Part1.B1, Part2.IN
  GND: Part1.GND, Part2.GND
  N2: Part1.Vout, Part2.VDD

custom parts:
  GEMMA v2: Love FLORA but want a bite-sized version? Look no further, GEMMA is a tiny wearable platform board with a lot of might in a 1" diameter package. Powered by a Attiny85 and programmable with an Arduino IDE over USB, you'll be able to realize any wearable project! We wanted to design a microcontroller board that was small enough to fit into any project, and low cost enough to use without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
  NeoPixel Jewel: We fit seven of our tiny 5050 (5mm x 5mm) smart RGB LEDs onto a beautiful, round PCB with mounting holes and a chainable design to create what we think is our most elegant (and evening-wear appropriate) NeoPixel board yet. Use only one microcontroller pin to control as many as you can chain together! Each LED is addressable as the driver chip is inside the LED. Each one has ~18mA constant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
