# Fritzing sketch LED_Candles (saved by Fritzing 0.9.3b)

parts:
  Part1 = GEMMA v2
  NeoPixel_Through-Hole = RGB LED (com. anode, rbg) [package="5 mm [THT]"]

nets:
  N1: Part1.B0, NeoPixel_Through-Hole.red_cathode
  N2: Part1.GND, NeoPixel_Through-Hole.blue_cathode
  N3: Part1.Vout, NeoPixel_Through-Hole.common_anode

custom parts:
  GEMMA v2: Love FLORA but want a bite-sized version? Look no further, GEMMA is a tiny wearable platform board with a lot of might in a 1" diameter package. Powered by a Attiny85 and programmable with an Arduino IDE over USB, you'll be able to realize any wearable project! We wanted to design a microcontroller board that was small enough to fit into any project, and low cost enough to use without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
