# Fritzing sketch thermo-clock (saved by Fritzing 0.9.3b)
breadboards: 1

parts:
  Part1 = Adafruit T-Cobbler Plus [part_number="Adafruit #1989 and #2028"]
  Part2 = Seven-Segment LED Backpack 1.2 Inch Digits [part_number=1269]
  DS1 = DS18B20 1-Wire Temperature Sensor [part_number=DS18B20]
  U1 = SWITCH_SPDT [package=kps-1290]
  R1 = Resistor [tolerance=±5% resistance=4.7k package=THT]
  Part4 = Adafruit DS1307 RTC Breakout [part_number="Adafruit #264"]

nets:
  N1: Part1.SDA, Part2.SDA, Part4.SQW
  N2: Part1.SCL, Part2.SCL, Part4.SCL
  N3: Part1.GPIO4, DS1.DQ, R1.Pin_0
  GND: Part1.GND, Part2.GND, DS1.GND, U1.O, Part4.GND
  N4: Part1.+3.3V_2, Part2.VCCIO, DS1.VDD, U1.S, R1.Pin_1
  +5V: Part1.+5V, Part2.VDD, Part4.VCC
  N5: Part1.GPIO18, U1.P

custom parts:
  Adafruit T-Cobbler Plus: The Raspberry Pi has landed on the Maker World like a 40-GPIO pinned, quad-USB ported, credit card sized bomb of DIY joy. And while you can use most of our great Model B accessories by hooking up our downgrade cable, its probably a good time to upgrade your set up and accessorize using all of the 40 pins. That's why we now carry the Assembled Adafruit Pi T-Cobbler Plus - Breakout + Cable for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
  Seven-Segment LED Backpack 1.2 Inch Digits: This jumbo 1.2" 7-segment LED display includes a driver chip for simple control via an I2C interface. The backpack features address-selection jumpers so you can connect up to eight displays on a single I2C bus.
  Adafruit DS1307 RTC Breakout: This is a great battery-backed real time clock (RTC) that allows your microcontroller project to keep track of time even if it is reprogrammed, or if the power is lost. Perfect for datalogging, clock-building, time stamping, timers and alarms, etc. The DS1307 is the most popular RTC - but it requires 5V power to work (although we've used it with 5V power and 3.3V logic successfully) PCB &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
