# Fritzing sketch circuit_diagram (saved by Fritzing 0.9.3b)

parts:
  Part1 = NeoPixel Jewel [part_number=2226]
  Part2 = Adafruit Feather M4 Express [part_number="Adafruit #3857"]
  Part3 = 24 NeoPixel Ring [part_number=1586]
  S1 = SPST Switch [package=switch-spdt_lock.007s]
  S2 = Round Pushbutton
  LED1 = RGB LED - (4 legs) [package="5 mm [THT]"]

nets:
  GND: Part1.GND, Part2.GND, Part3.GND, S1.P, S2.leg1
  N1: Part1.IN, Part3.OUT
  VDD: Part1.VDD, Part2.+3V3, Part3.VDD, LED1.common_anode
  N2: Part2.EN, S1.O
  N3: Part2.D12, S2.leg0
  N4: Part2.D11, LED1.blue_cathode
  N5: Part2.D10, LED1.green_cathode
  N6: Part2.D9, LED1.red_cathode
  N7: Part2.D6, Part3.IN

custom parts:
  NeoPixel Jewel: We fit seven of our tiny 5050 (5mm x 5mm) smart RGB LEDs onto a beautiful, round PCB with mounting holes and a chainable design to create what we think is our most elegant (and evening-wear appropriate) NeoPixel board yet. Use only one microcontroller pin to control as many as you can chain together! Each LED is addressable as the driver chip is inside the LED. Each one has ~18mA constant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
  Adafruit Feather M4 Express: It's what you've been waiting for, the Feather M4 Express featuring ATSAMD51. This Feather is fast like a swift, smart like an owl, strong like a ox-bird (it's half ox, half bird, OK?) This feather is powered by our new favorite chip, the ATSAMD51J19 - with its 120MHz Cortex M4 with floating point support and 512KB Flash and 192KB RAM. Your code will zig and zag and zoom, and with a bunch of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
  24 NeoPixel Ring: 24 ultra bright smart LED NeoPixels are arranged in a circle with 2.6" (66mm) outer diameter. The rings are 'chainable' - connect the output pin of one to the input pin of another. Use only one microcontroller pin to control as many as you can chain together! Each LED is addressable as the driver chip is inside the LED. Each one has ~18mA constant current drive so the color will be very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
