# Fritzing sketch NeoPixie_Dust_Bag (saved by Fritzing 0.9.3b)
circuit board: 10.8467cm x 5.64444cm
breadboards: 1

parts:
  neopixel12 = Neopixel Ring 12
  neopixel16 = Neopixel Ring 16
  BATT = LiPoly Battery (1300mAh)
  R1 = Resistor [tolerance=±5% resistance=10k package=THT]
  CAPSENSE = AT42QT1010 Momentary Capsense Breakout
  S1 = Toggle Switch [package=THT]
  GEMMA = Adafruit GEMMA
  Part1 = GEMMA v2  # not connected
  LED1 = prefix0000
  LED2 = prefix0000

nets:
  GND: neopixel12.GND, neopixel16.GND, LED2.connector3
  VCC: neopixel12.VCC, neopixel16.VCC, GEMMA.Vout
  N1: neopixel12.IN, LED2.connector4
  N2: neopixel12.OUT, neopixel16.IN
  N3: BATT.positive, S1.L2
  N4: BATT.negative, R1.Pin_1, CAPSENSE.GND
  N5: R1.Pin_0, CAPSENSE.OUT, GEMMA.D2/A1
  N6: CAPSENSE.VDD, S1.COM
  N7: GEMMA.D0, LED1.connector2
  N8: LED1.connector1, LED2.connector1
  N9: LED1.connector4, LED2.connector2

custom parts:
  Neopixel Ring 12: Neopixel Ring x12
  Neopixel Ring 16: Neopixel Ring x16
  LiPoly Battery (1300mAh): Lithium Ion Polymer Battery (1300mAh)
  AT42QT1010 Momentary Capsense Breakout: A capacitive touch momentary switch breakout for the AT42QT1010 chip.
  Adafruit GEMMA: Adafruit Gemma wearable electronics main board.
  GEMMA v2: Love FLORA but want a bite-sized version? Look no further, GEMMA is a tiny wearable platform board with a lot of might in a 1" diameter package. Powered by a Attiny85 and programmable with an Arduino IDE over USB, you'll be able to realize any wearable project! We wanted to design a microcontroller board that was small enough to fit into any project, and low cost enough to use without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
