# Fritzing sketch circuit diagram (saved by Fritzing 0.9.3b)

parts:
  Part1 = Adafruit NeoTrellis 4x4 [part_number=https://www.adafruit.com/product/3954]
  BUTTON1 = Waterproof Pushbutton (red)
  Part2 = Adafruit Feather M0 Express [part_number="Adafruit #3403"]
  S2 = Toggle Switch [package=THT]

nets:
  N1: Part1.INT, Part2.D5
  VIN: Part1.VIN, BUTTON1.no_name_yet#4, Part2.+3V3
  GND: Part1.GND, BUTTON1.no_name_yet#1, BUTTON1.no_name_yet#5, Part2.GND, S2.COM
  N2: Part1.SCL, Part2.SCL
  N3: Part1.SDA, Part2.SDA
  N4: BUTTON1.no_name_yet#2, Part2.D6
  N5: Part2.EN, S2.L2

custom parts:
  Waterproof Pushbutton (red): Waterproof Illuminated Pushbutton (red)
  Adafruit Feather M0 Express: We love all our Feathers equally, but this Feather is very special. It's our first Feather that is specifically designed for use with CircuitPython! CircuitPython is our beginner-oriented flavor of MicroPython - and as the name hints at, its a small but full-featured version of the popular Python programming language specifically for use with circuitry and electronics. That doesn't mean you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
