# Fritzing sketch m0_analog_rgb (saved by Fritzing 0.9.3b)
breadboards: 1

parts:
  Q1 = Basic FET N-Channel [package="DPak [SMD]"]
  Q2 = Basic FET N-Channel [package="DPak [SMD]"]
  Q3 = Basic FET N-Channel [package="DPak [SMD]"]
  Part1 = Adafruit Metro M0 Express
  JACK1 = 2.1mm Barrel Jack with Terminal Block

nets:
  N1: Q1.Gate, Part1.D6
  N2: Q1.source, Q2.source, Q3.source, Part1.GND, JACK1.NEG
  N3: Q2.Gate, Part1.D5
  N4: Q3.Gate, Part1.D3

notes:
  To 12V power supply

custom parts:
  Adafruit Metro M0 Express: Metro is our series of microcontroller boards for use with the Arduino IDE. This new Metro board looks a whole lot like our original Metro 328, but with a huge upgrade. Instead of the ATmega328, this Metro features a ATSAMD21G18 chip, an ARM Cortex M0+. It's our first Metro that is designed for use with CircuitPython! CircuitPython is our beginner-oriented flavor of MicroPython - and as the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
