# Fritzing sketch ds18b20-basic-20pin (saved by Fritzing 0.9.3b)
breadboards: 1

parts:
  DS1 = DS18B20 1-Wire Temperature Sensor [part_number=DS18B20]
  R1 = Resistor [tolerance=±5% resistance=4.7 package=THT]
  Part1 = Adafruit Pi Cobbler [part_number="Adafruit #914"]

nets:
  VDD: DS1.VDD, R1.Pin_0, Part1.3.3V
  N1: DS1.DQ, R1.Pin_1, Part1.GPIO4
  GND: DS1.GND, Part1.GND

custom parts:
  Adafruit Pi Cobbler: Now that you've finally got your hands on a Raspberry Pi® Model B , you're probably itching to make some fun embedded computer projects with it. What you need is an add on prototyping Pi Cobbler from Adafruit, which can break out all those tasty power, GPIO, I2C and SPI pins from the 26 pin header onto a solderless breadboard. This set will make "cobbling together" prototypes with the Pi super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
