# Fritzing sketch ds18b20-waterproof-40pin (saved by Fritzing 0.9.3b)
breadboards: 1

parts:
  R1 = Resistor [tolerance=±5% resistance=4.7 package=THT]
  DS1 = DS18B20 1-Wire Temperature Sensor Probe Cable
  Part1 = Adafruit Pi Cobbler Plus [part_number="Adafruit #2029"]

nets:
  VDD: R1.Pin_0, DS1.VDD, Part1.+3.3V
  N1: R1.Pin_1, DS1.shield, Part1.GPIO4
  GND: DS1.GND, Part1.GND

custom parts:
  Adafruit Pi Cobbler Plus: The Raspberry Pi B+/Pi 2/ Pi 3 has landed on the Maker World like a 40-GPIO pinned, quad-USB ported, credit card sized bomb of DIY joy. And while you can use most of our great Model B accessories by hooking up our downgrade cable, its probably a good time to upgrade your set up and accessorize using all of the Model B+'s / Pi 2's / Pi 3's 40 pins. That's why we now carry the Adafruit Assembled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
