# Fritzing sketch Raspberry_Pi_Power_Control (saved by Fritzing 0.9.3b)
breadboards: 1

parts:
  SW1 = PowerSwitch Tail II
  PIR1 = PIR sensor
  Part1 = Adafruit Pi Cobbler Plus [part_number="Adafruit #2029"]

nets:
  N1: SW1.+in, Part1.GPIO23
  GND: SW1.-in, PIR1.GND, Part1.GND
  VDD: PIR1.VDD, Part1.+5V
  N2: PIR1.SIG, Part1.GPIO24

custom parts:
  Adafruit Pi Cobbler Plus: The Raspberry Pi B+/Pi 2/ Pi 3 has landed on the Maker World like a 40-GPIO pinned, quad-USB ported, credit card sized bomb of DIY joy. And while you can use most of our great Model B accessories by hooking up our downgrade cable, its probably a good time to upgrade your set up and accessorize using all of the Model B+'s / Pi 2's / Pi 3's 40 pins. That's why we now carry the Adafruit Assembled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
