# Fritzing sketch Raspberry_Pi_Sensing_Movement-Cobbler-20pin (saved by Fritzing 0.9.3b)
breadboards: 1

parts:
  PIR2 = PIR sensor
  S2 = Magnetic Door Switch [package=reed_switch_plastic]
  Part1 = Adafruit Pi Cobbler [part_number="Adafruit #914"]

nets:
  N1: PIR2.VDD, Part1.5.0V
  N2: PIR2.SIG, Part1.GPIO18
  GND: PIR2.GND, S2.1, Part1.GND
  N3: S2.2, Part1.GPIO23

custom parts:
  Adafruit Pi Cobbler: Now that you've finally got your hands on a Raspberry Pi® Model B , you're probably itching to make some fun embedded computer projects with it. What you need is an add on prototyping Pi Cobbler from Adafruit, which can break out all those tasty power, GPIO, I2C and SPI pins from the 26 pin header onto a solderless breadboard. This set will make "cobbling together" prototypes with the Pi super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
