# Fritzing sketch Raspberry_Pi_Sensing_Movement-Cobbler-Plus-40pin (saved by Fritzing 0.9.3b)
breadboards: 1

parts:
  Part1 = Adafruit Pi Cobbler Plus [part_number="Adafruit #2029"]
  PIR1 = PIR sensor
  S1 = Magnetic Door Switch [package=reed_switch_plastic]

nets:
  GND: Part1.GND, PIR1.GND, S1.1
  +5V: Part1.+5V, PIR1.VDD
  N1: Part1.GPIO18, PIR1.SIG
  N2: Part1.GPIO23, S1.2

custom parts:
  Adafruit Pi Cobbler Plus: The Raspberry Pi B+/Pi 2/ Pi 3 has landed on the Maker World like a 40-GPIO pinned, quad-USB ported, credit card sized bomb of DIY joy. And while you can use most of our great Model B accessories by hooking up our downgrade cable, its probably a good time to upgrade your set up and accessorize using all of the Model B+'s / Pi 2's / Pi 3's 40 pins. That's why we now carry the Adafruit Assembled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
