# Fritzing sketch Raspberry_Pi_Stepper_Motors-Cobbler-Plus-ULN2803A (saved by Fritzing 0.9.3b)
breadboards: 1

parts:
  Part1 = Adafruit Pi Cobbler Plus [part_number="Adafruit #2029"]
  IC1 = ULN2803A [package=THT]
  MOTOR1 = Adafruit Gear-Reduced Stepper Motor (small)

nets:
  N1: Part1.GPIO4, IC1.In_1
  N2: Part1.GND, IC1.0V
  N3: Part1.GPIO17, IC1.In_2
  N4: Part1.+5V, IC1.COM_-_Common, MOTOR1.RED
  N5: Part1.GPIO23, IC1.In_3
  N6: Part1.GPIO24, IC1.In_4
  N7: IC1.Out_4, MOTOR1.YELLOW
  N8: IC1.Out_3, MOTOR1.BLUE
  N9: IC1.Out_2, MOTOR1.ORANGE
  N10: IC1.Out_1, MOTOR1.PINK

custom parts:
  Adafruit Pi Cobbler Plus: The Raspberry Pi B+/Pi 2/ Pi 3 has landed on the Maker World like a 40-GPIO pinned, quad-USB ported, credit card sized bomb of DIY joy. And while you can use most of our great Model B accessories by hooking up our downgrade cable, its probably a good time to upgrade your set up and accessorize using all of the Model B+'s / Pi 2's / Pi 3's 40 pins. That's why we now carry the Adafruit Assembled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
  Adafruit Gear-Reduced Stepper Motor (small): Adafruit gear-reduction stepper motor (small)
