# Fritzing sketch Raspberry_Pi_Stepper_Motors-T-Cobbler-Plus-L293D (saved by Fritzing 0.9.3b)
breadboards: 1

parts:
  Part1 = Adafruit T-Cobbler Plus [part_number="Adafruit #1989 and #2028"]
  IC1 = L293D [package=THT]
  MOTOR1 = Adafruit Gear-Reduced Stepper Motor (small)

nets:
  N1: Part1.GPIO4, IC1.In_1
  N2: Part1.GND, IC1.0V
  N3: Part1.GPIO17, IC1.In_2
  N4: Part1.+5V, IC1.+Vmotor, IC1.+V
  N5: Part1.GPIO18, IC1.Enable_1, IC1.Enable_2
  N6: Part1.GPIO23, IC1.In_4
  N7: Part1.GPIO24, IC1.In_3
  N8: IC1.Out_1_(_Controlled_by_Enable_1_), MOTOR1.PINK
  N9: IC1.Out_2_(_Controlled_by_Enable_1_), MOTOR1.ORANGE
  N10: IC1.Out_3_(_Controlled_by_Enable_2_), MOTOR1.YELLOW
  N11: IC1.Out_4_(_Controlled_by_Enable_2_), MOTOR1.BLUE

custom parts:
  Adafruit T-Cobbler Plus: The Raspberry Pi has landed on the Maker World like a 40-GPIO pinned, quad-USB ported, credit card sized bomb of DIY joy. And while you can use most of our great Model B accessories by hooking up our downgrade cable, its probably a good time to upgrade your set up and accessorize using all of the 40 pins. That's why we now carry the Assembled Adafruit Pi T-Cobbler Plus - Breakout + Cable for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
  Adafruit Gear-Reduced Stepper Motor (small): Adafruit gear-reduction stepper motor (small)
