# Fritzing sketch screamingCauldron (saved by Fritzing 0.9.3b)
breadboards: 1

parts:
  Part1 = Adafruit Trinket M0 [part_number="Adafruit #3500"]
  Part2 = Audio FX Sound Board
  NEOPIXEL1 = Neopixel Strip -- Black (30/m)
  BATT1 = 4xAA Switchable Battery Pack w/JST connector
  C1 = Capacitor Polarized [package=cpol-radial-1000uf-63v]
  J1 = Infrared Proximity Sensor
  R1 = Resistor [tolerance=±5% resistance=470 package="2010 [SMD]"]

nets:
  VIN: Part1.VBAT, Part2.VIN, NEOPIXEL1.+5V, BATT1.POS, C1.+, J1.Vcc
  GND: Part1.GND, Part2.GND, NEOPIXEL1.GND, BATT1.NEG, C1.-, J1.GND
  N1: Part1.D2_A1_PA09_SCL_MISO, Part2.0
  N2: Part1.D1_A0_PA02, J1.Vout
  N3: Part1.D0_A4_PA08_SDA, R1.Pin_0
  N4: NEOPIXEL1.Din, R1.Pin_1

custom parts:
  Audio FX Sound Board: The Adafruit Sound Board, the fastest way to add audio effects to a project!
  Neopixel Strip -- Black (30/m): These NeoPixel strips have 30 digitally-addressable pixel LEDs per meter and are very affordable and are only 12.5 mm wide, 10 mm if you remove the strip from the casing.
  4xAA Switchable Battery Pack w/JST connector: 4xAA Switchable Battery Pack with JST connector
