# Fritzing sketch m0_adalogger_ttl_camera (saved by Fritzing 0.9.3b)

parts:
  Part1 = Adafruit Feather M0 Adalogger [part_number="Adafruit #2796"]
  CAMERA1 = TTL Serial JPEG Camera

nets:
  N1: Part1.D1, CAMERA1.TX
  N2: Part1.D0, CAMERA1.RX
  GND: Part1.GND, CAMERA1.GND
  N3: Part1.VBUS, CAMERA1.5V

custom parts:
  Adafruit Feather M0 Adalogger: This is the Adafruit Feather M0 Adalogger - our take on an 'all-in-one' Cortex M0 datalogger (or data-reader) with built in USB and battery charging. Its an Adafruit Feather M0 with a microSD holder ready to rock! We have other boards in the Feather family, check'em out here At the Feather M0's heart is an ATSAMD21G18 ARM Cortex M0 processor, clocked at 48 MHz and at 3.3V logic, the same one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
  TTL Serial JPEG Camera: TTL Serial JPEG Camera with NTSC Out
