# Fritzing sketch Textile_Potentiometer_Hoodie (saved by Fritzing 0.9.3b)

parts:
  Part1 = GEMMA v2
  LED1 = prefix0000
  BATT1 = 3xAAA Switchable Battery Pack w/JST connector  # not connected
  R1 = Textile Potentiometer [part_number=PW064]

nets:
  N1: Part1.3.3V, R1.leg2
  N2: Part1.B1, LED1.connector2
  N3: Part1.B2, R1.wiper
  N4: Part1.GND, LED1.connector3, R1.leg1
  N5: Part1.Vout, LED1.connector1

custom parts:
  GEMMA v2: Love FLORA but want a bite-sized version? Look no further, GEMMA is a tiny wearable platform board with a lot of might in a 1" diameter package. Powered by a Attiny85 and programmable with an Arduino IDE over USB, you'll be able to realize any wearable project! We wanted to design a microcontroller board that was small enough to fit into any project, and low cost enough to use without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
  3xAAA Switchable Battery Pack w/JST connector: 3xAAA Switchable Battery Pack with JST connector
