# Fritzing sketch Gemma_Blinky_Eyes (saved by Fritzing 0.9.3b)
breadboards: 1

parts:
  LED1 = LED - 5mm [color="Red (633nm)" package="5 mm [THT]"]
  LED2 = LED - 5mm [color="Red (633nm)" package="5 mm [THT]"]
  R1 = PHOTOCELL [package=photocell]
  R2 = Resistor [tolerance=±5% resistance=1k package="1206 [SMD]"]
  Part1 = GEMMA v2

nets:
  N1: LED1.cathode, LED2.cathode, Part1.B0
  N2: LED1.anode, LED2.anode, R2.Pin_0, Part1.GND
  N3: R1.P$1, Part1.3.3V
  N4: R1.P$2, R2.Pin_1, Part1.B2

custom parts:
  GEMMA v2: Love FLORA but want a bite-sized version? Look no further, GEMMA is a tiny wearable platform board with a lot of might in a 1" diameter package. Powered by a Attiny85 and programmable with an Arduino IDE over USB, you'll be able to realize any wearable project! We wanted to design a microcontroller board that was small enough to fit into any project, and low cost enough to use without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
