# Fritzing sketch Trinket_Blinky_Eyes (saved by Fritzing 0.9.3b)
breadboards: 1

parts:
  LED1 = LED - 5mm [color="Red (633nm)" package="5 mm [THT]"]
  LED2 = LED - 5mm [color="Red (633nm)" package="5 mm [THT]"]
  Part1 = Adafruit Trinket M0 [part_number="Adafruit #3500"]
  R1 = PHOTOCELL [package=photocell]
  R2 = Resistor [tolerance=±5% resistance=1k package="1206 [SMD]"]

nets:
  N1: LED1.cathode, LED2.cathode, Part1.D0_A4_PA08_SDA
  N2: LED1.anode, LED2.anode, Part1.GND, R2.Pin_0
  N3: Part1.3.3V, R1.P$1
  N4: Part1.D2_A1_PA09_SCL_MISO, R1.P$2, R2.Pin_1
