# Fritzing sketch Trinket_Question_Block_Sound_Jewelry (saved by Fritzing 0.9.3b)

parts:
  Part1 = Adafruit Trinket M0 [part_number="Adafruit #3500"]
  Part4 = LED Sequin - Warm White [part_number=1758]
  Part5 = LED Sequin - Warm White [part_number=1758]
  Part6 = Adafruit Pro Trinket LiIon/LiPoly Backpack [part_number="Adafruit #2124"]
  J1 = Piezo Speaker
  S1 = Tilt Switch [package=THT]
  U1 = SWITCH_SPDT [package=kps-1290]

nets:
  N1: Part1.VBAT, Part6.VBAT
  GND: Part1.GND, Part4.-, Part5.-, Part6.GND
  N2: Part1.D4_A2_PA06_TXD_MOSI, Part4.+, Part5.+
  N3: Part1.D2_A1_PA09_SCL_MISO, J1.pin2
  N4: Part1.D1_A0_PA02, S1.Pin_1
  N5: Part1.VBUS, Part6.VBUS
  N6: Part6.SW2, U1.S
  N7: Part6.SW1, U1.P

notes:
  To "-" pad on back of Trinket M0

custom parts:
  LED Sequin - Warm White: Sew a little sparkle into your wearable project with an Adafruit LED Sequin. Simply connect 3 to 6VDC to the + pin and ground to the - pin, and the LED on the board will light up. You can make the LEDs fade and twinkle by using PWM.
  Adafruit Pro Trinket LiIon/LiPoly Backpack: If you have a Pro Trinket you probably know it's the perfect little size for a portable project. This LiPoly backpack makes it really easy to do! Instead of wiring 2 or 3 boards together to make a charging system, this little PCB sits on top of the Pro Trinket and allows a LiPoly/LiIon battery to plug in. When the Pro Trinket USB port is powered, the battery is recharged automatically. Unplug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
