# Fritzing sketch neoMatrix (saved by Fritzing 0.9.3b)

parts:
  Part1 = Adafruit Metro with Headers [part_number="Adafruit #2488"]
  J1 = Piezo Speaker
  S1 = Square Pushbutton
  LED1 = LED - 5mm [color="Yellow (585nm)" package="5 mm [THT]"]

nets:
  N1: Part1.AD1, J1.pin2
  N2: Part1.GND, J1.pin1, S1.leg0, LED1.cathode
  N3: Part1.SCK, LED1.anode
  N4: Part1.MOSI, S1.leg1

custom parts:
  Adafruit Metro with Headers: We sure love the ATmega328 here at Adafruit, and we use them a lot for our own projects. The processor has plenty of GPIO, Analog inputs, hardware UART SPI and I2C, timers and PWM galore - just enough for most simple projects. When we need to go small, we use a Pro Trinket 3V or 5V, but when size isn't as much of a concern, and an USB-serial converter is required, we reach for an Adafruit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
