# Fritzing sketch rfm69 (saved by Fritzing 0.9.3b)
breadboards: 1

parts:
  Part2 = Adafruit T-Cobbler Plus [part_number="Adafruit #1989 and #2028"]
  S1 = Pushbutton [package="[THT]"]
  S2 = Pushbutton [package="[THT]"]
  S3 = Pushbutton [package="[THT]"]
  Part6 = OLED Monochrome 128x32 I2C [part_number=931]
  Part7 = Adafruit RFM69HCW Transceiver Radio [part_number="Adafruit #3070 and #3071"]

nets:
  VIN: Part2.+3.3V, Part6.VIN, Part7.VIN
  N1: Part2.SDA, Part6.SDA
  N2: Part2.SCL, Part6.SCL
  N3: Part2.GPIO4, Part6.RESET
  GND: Part2.GND, S1.Pin_1, S1.Pin_2, S2.Pin_1, S2.Pin_2, S3.Pin_3, S3.Pin_4, Part6.GND, Part7.GND
  N4: Part2.MOSI, Part7.MOSI
  N5: Part2.MISO, Part7.MISO
  N6: Part2.SCLK, Part7.SCK
  N7: Part2.GPIO5, S3.Pin_1, S3.Pin_2, Part7.DIO0
  N8: Part2.GPIO6, S1.Pin_3, S1.Pin_4
  N9: Part2.GPIO25, Part7.RST
  N10: Part2.CE1, Part7.CS
  N11: Part2.GPIO12, S2.Pin_3, S2.Pin_4
  N12: Part7.DIO1, Part7.DIO2, Part7.DIO3, Part7.DIO4, Part7.DIO5

custom parts:
  Adafruit T-Cobbler Plus: The Raspberry Pi has landed on the Maker World like a 40-GPIO pinned, quad-USB ported, credit card sized bomb of DIY joy. And while you can use most of our great Model B accessories by hooking up our downgrade cable, its probably a good time to upgrade your set up and accessorize using all of the 40 pins. That's why we now carry the Assembled Adafruit Pi T-Cobbler Plus - Breakout + Cable for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
  OLED Monochrome 128x32 I2C: These displays are small, only about 1" diagonal, but very readable due to the high contrast of an OLED display. This display is made of 128x32 individual white OLED pixels, each one is turned on or off by the controller chip. Because the display makes its own light, no backlight is required. This reduces the power required to run the OLED and is why the display has such high contrast; we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
  Adafruit RFM69HCW Transceiver Radio: Sending data over long distances is like magic, and now you can be a magician with this range of powerful and easy-to-use radio modules. Sure, sometimes you want to talk to a computer (a good time to use WiFi) or perhaps communicate with a Phone (choose Bluetooth Low Energy!) but what if you want to send data very far? Most WiFi, Bluetooth, Zigbee and other wireless chipsets use 2.4GHz, which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
